// Digital circuit main.dig as structural Verilog
module main (
);

  wire ADDR_RS0_A, ADDR_RS0_B, ADDR_RS0_C, ADDR_RS0_D, ADDR_RS1_A, ADDR_RS1_B, ADDR_RS1_C, ADDR_RS1_D,
       alu_1_p1, ALU_A_IN_A, ALU_A_IN_B, ALU_B_IN_A, ALU_B_IN_B, ALU_C_IN_A, ALU_C_IN_B, ALU_D_IN_A,
       ALU_D_IN_B, DB_RD_DEV, imm8, imm16, instruction_decoder_1_p3, instruction_decoder_1_p8,
       instruction_decoder_1_p15, IR0_RD, IR1_RD, IR2_RD, nand_1_out, ooo, or_1_out, PC_2_ovf, PC_H_RD,
       PC_INC, PC_L_RD, PC_ovf, PC_WR_AB, REG_A_RD, REG_B_RD, REG_C_RD, REG_D_RD, RS_WR_AB, SP_DEC, SP_H_RD,
       SP_INC, SP_L_RD, SP_WR_AB, undriven, undriven_2, undriven_3;
  wire [1:0] ll, rs1;
  wire [2:0] REG_RD, rs0, vvv;
  wire [3:0] alu_1_p6, alu_1_p7;
  wire [7:0] A_q, ACC_q, alu_1_p5, B_q, C_q, D_q, driver_3_out, driver_19_out, instruction_decoder_1_p1,
       instruction_decoder_1_p7, instruction_decoder_1_p10, IR0_D, PC_2_hi, PC_2_lo, PC_hi, PC_lo;
  wire [15:0] driver_1_out, driver_8_out;

  CounterPreset counterpreset_1 ();  // open: en, C, dir, in, ld, clr, out, ovf
  // microcode microcode_1: pin names not known; wires that end beside it: IR0_D, PC_INC, PC_L_RD, PC_H_RD, IR0_RD, IR1_RD, IR2_RD, PC_WR_AB, SP_WR_AB, SP_INC, SP_DEC, RS_WR_AB, REG_RD, DB_RD_DEV
  or or_1 (or_1_out, SP_DEC, SP_INC);
  _16_bit_presettable_counter PC (
    .en(PC_INC), .dir(1'b0), .lo_in(instruction_decoder_1_p1), .lo_ld(PC_L_RD),
    .hi_in(instruction_decoder_1_p1), .hi_ld(PC_H_RD), .clr(1'b0), .ovf(PC_ovf), .lo(PC_lo), .hi(PC_hi));  // open: c
  _16_bit_presettable_counter PC_2 (
    .en(or_1_out), .dir(SP_DEC), .lo_in(instruction_decoder_1_p1), .lo_ld(SP_L_RD),
    .hi_in(instruction_decoder_1_p1), .hi_ld(SP_H_RD), .clr(1'b0), .ovf(PC_2_ovf), .lo(PC_2_lo), .hi(PC_2_hi));  // open: c
  LED led_1 (.in(PC_ovf));
  assign driver_1_out = PC_WR_AB ? {PC_hi, PC_lo} : 16'bz;  // Driver driver_1
  LED led_2 (.in(PC_2_ovf));
  assign driver_1_out = SP_WR_AB ? {PC_2_hi, PC_2_lo} : 16'bz;  // Driver driver_2
  Driver driver_3 (.in(PC_2_lo[0]), .out(driver_3_out[0]));  // open: en
  Driver driver_4 (.in(PC_2_hi[0]), .out(driver_3_out[0]));  // open: en
  assign driver_1_out[0] = RS_WR_AB ? driver_8_out[0] : 1'bz;  // Driver driver_5
  Register #(.Bits(8)) IR0 (.D(instruction_decoder_1_p1), .C(instruction_decoder_1_p3), .en(IR0_RD), .Q(IR0_D));
  Register #(.Bits(8)) A (.D(instruction_decoder_1_p1), .en(REG_A_RD), .Q(A_q));  // open: C
  Register #(.Bits(8)) B (.D(instruction_decoder_1_p1), .en(REG_B_RD), .Q(B_q));  // open: C
  Register #(.Bits(8)) C (.D(instruction_decoder_1_p1), .en(REG_C_RD), .Q(C_q));  // open: C
  Register #(.Bits(8)) D (.D(instruction_decoder_1_p1), .en(REG_D_RD), .Q(D_q));  // open: C
  // instruction_decoder instruction_decoder_1: pin names not known; wires that end beside it: instruction_decoder_1_p1, driver_1_out, instruction_decoder_1_p3, ll, IR0_D, ooo, instruction_decoder_1_p7, instruction_decoder_1_p8, vvv, instruction_decoder_1_p10, imm8, rs0, rs1, imm16, instruction_decoder_1_p15
  Register #(.Bits(8)) IR1 (
    .D(instruction_decoder_1_p1), .C(instruction_decoder_1_p8), .en(IR1_RD), .Q(instruction_decoder_1_p7));
  assign instruction_decoder_1_p1 = undriven_3 ? A_q : 8'bz;  // Driver driver_6
  assign driver_8_out[7:0] = ADDR_RS1_A ? A_q : 8'bz;  // Driver driver_7
  assign driver_8_out[15:8] = ADDR_RS0_A ? A_q : 8'bz;  // Driver driver_8
  assign instruction_decoder_1_p1 = undriven_2 ? B_q : 8'bz;  // Driver driver_9
  assign driver_8_out[7:0] = ADDR_RS1_B ? B_q : 8'bz;  // Driver driver_10
  assign driver_8_out[15:8] = ADDR_RS0_B ? B_q : 8'bz;  // Driver driver_11
  assign instruction_decoder_1_p1 = undriven ? C_q : 8'bz;  // Driver driver_12
  assign driver_8_out[7:0] = ADDR_RS1_C ? C_q : 8'bz;  // Driver driver_13
  assign driver_8_out[15:8] = ADDR_RS0_C ? C_q : 8'bz;  // Driver driver_14
  assign instruction_decoder_1_p1 = alu_1_p1 ? D_q : 8'bz;  // Driver driver_15
  assign driver_8_out[7:0] = ADDR_RS1_D ? D_q : 8'bz;  // Driver driver_16
  assign driver_8_out[15:8] = ADDR_RS0_D ? D_q : 8'bz;  // Driver driver_17
  Register #(.Bits(8)) IR2 (
    .D(instruction_decoder_1_p1), .C(instruction_decoder_1_p15), .en(IR2_RD), .Q(instruction_decoder_1_p10));
  assign driver_3_out = ALU_A_IN_B ? A_q : 8'bz;  // Driver driver_18
  assign driver_19_out = ALU_A_IN_A ? A_q : 8'bz;  // Driver driver_19
  assign driver_3_out = ALU_B_IN_B ? B_q : 8'bz;  // Driver driver_20
  assign driver_19_out = ALU_B_IN_A ? B_q : 8'bz;  // Driver driver_21
  assign driver_3_out = ALU_C_IN_B ? C_q : 8'bz;  // Driver driver_22
  assign driver_19_out = ALU_C_IN_A ? C_q : 8'bz;  // Driver driver_23
  assign driver_3_out = ALU_D_IN_B ? D_q : 8'bz;  // Driver driver_24
  assign driver_19_out = ALU_D_IN_A ? D_q : 8'bz;  // Driver driver_25
  Driver #(.Bits(8)) driver_26 (.in(alu_1_p5), .out(instruction_decoder_1_p1));  // open: en
  Driver driver_27 (.in(imm8), .out(driver_3_out[0]));  // open: en
  // alu alu_1: pin names not known; wires that end beside it: alu_1_p1, ooo, driver_3_out, driver_19_out, alu_1_p5, alu_1_p6, alu_1_p7
  nand nand_1 (nand_1_out, ll[0], ll[1]);
  assign driver_19_out = nand_1_out ? ACC_q : 8'bz;  // Driver driver_28
  Driver #(.Bits(8)) driver_29 (.in(ACC_q), .out(instruction_decoder_1_p1));  // open: en
  Register #(.Bits(4)) Flag (.D(alu_1_p7), .Q(alu_1_p6));  // open: C, en
  Decoder #(.Selector_Bits(2)) decoder_1 (
    .sel(vvv[1:0]), .out_0(ALU_A_IN_B), .out_1(ALU_B_IN_B), .out_2(ALU_C_IN_B), .out_3(ALU_D_IN_B));
  Decoder #(.Selector_Bits(2)) decoder_2 (
    .sel(rs0[1:0]), .out_0(ALU_A_IN_A), .out_1(ALU_B_IN_A), .out_2(ALU_C_IN_A), .out_3(ALU_D_IN_A));
  Register #(.Bits(8)) ACC (.D(instruction_decoder_1_p1), .Q(ACC_q));  // open: C, en
  Decoder #(.Selector_Bits(2)) decoder_3 (
    .sel(rs0[1:0]), .out_0(ADDR_RS0_A), .out_1(ADDR_RS0_B), .out_2(ADDR_RS0_C), .out_3(ADDR_RS0_D));
  Decoder #(.Selector_Bits(2)) decoder_4 (
    .sel(rs1), .out_0(ADDR_RS1_A), .out_1(ADDR_RS1_B), .out_2(ADDR_RS1_C), .out_3(ADDR_RS1_D));
  Decoder #(.Selector_Bits(3)) decoder_5 (
    .sel(REG_RD), .out_0(REG_A_RD), .out_1(REG_B_RD), .out_2(REG_C_RD), .out_3(REG_D_RD), .out_4(PC_L_RD),
    .out_5(PC_H_RD), .out_6(SP_L_RD), .out_7(SP_H_RD));
  // Pins of 1 and 8 bits meet at driver_3_out
  // Pins of 1 and 16 bits meet at driver_8_out
  // Pins of 1 and 16 bits meet at driver_1_out
  // Pins of 2 and 3 bits meet at rs0
  // Pins of 1 and 8 bits meet at PC_2_lo
  // Pins of 1 and 8 bits meet at PC_2_hi

  // Notes on the sheet:
  //   Stack Pointer
  //   Program Counter
  //   DBUS
  //   ABUS
  //   Instruction Register
  //   Registers
  //   Decoder
  //   ALU
  //   ALU BUS
  //   ALU Decoders
  //   ACC
  //   Flag register
  //   Address Decoders
endmodule
