// Digital circuit microcode.dig as structural Verilog
module microcode (
  input  [7:0] d0,
  input  c,
  output uPC_CLR,
  output PC_INC,
  output PCL_RD,
  output PCH_RD,
  output IR0_RD,
  output IR1_RD,
  output IR2_RD,
  output SP_INC,
  output SP_DEC,
  output [2:0] REG_RD,
  output [2:0] DB_WR_DEV,
  output [1:0] AB_WR_DEV
);

  wire [3:0] uPC_out;
  wire [7:1] rom_1_d;

  ROM #(.AddrBits(12), .Bits(8)) rom_1 (.A({uPC_out, d0}), .sel(1'b1), .D({rom_1_d, DB_WR_DEV[2]}));
  Counter #(.Bits(4)) uPC (.en(1'b1), .C(c), .clr(uPC_CLR), .out(uPC_out));  // open: ovf
  ROM #(.AddrBits(12), .Bits(8)) rom_2 (.A({uPC_out, d0}), .sel(1'b1), .D({DB_WR_DEV[1:0], REG_RD, AB_WR_DEV, SP_DEC}));
  ROM #(.AddrBits(12), .Bits(8)) rom_3 (
    .A({uPC_out, d0}), .sel(1'b1), .D({SP_INC, IR2_RD, IR1_RD, IR0_RD, PCH_RD, PCL_RD, PC_INC, uPC_CLR}));

  // Notes on the sheet:
  //   contents of rom_2 (hex, n*v repeats v):
  //   2
  //   contents of rom_3 (hex, n*v repeats v):
  //   6,1,254*0,1
endmodule
